# Fritzing sketch Untitled Sketch 2 (saved by Fritzing 0.9.3b)
breadboards: 1

parts:
  Parça1 = Arduino Mega 2560 (Rev3)
  Parça2 = RFID-RC522-v3
  Parça3 = Adafruit MicroSD card breakout board [part_number="Adafruit #254"]

nets:
  N1: Parça1.D9_PWM, Parça2.SDA
  N2: Parça1.D8_PWM, Parça2.RST
  3V3: Parça1.3V3, Parça2.3.3V
  GND: Parça1.GND, Parça2.GND
  N3: Parça1.D4_PWM, Parça3.CS
  N4: Parça1.D50, Parça2.MISO
  N5: Parça1.D51, Parça2.MOSI
  N6: Parça1.D52, Parça2.SCK

custom parts:
  RFID-RC522-v3: A simple China made RFID-RC522 Reader (6x4 cm); do check the pin labels, as this is a MFRC522 based clone.
  Adafruit MicroSD card breakout board: Not just a simple breakout board, this microSD adapter goes the extra mile - designed for ease of use. Onboard 5v->3v regulator provides 150mA for power-hungry cards 3v level shifting means you can use this with ease on either 3v or 5v systems Uses a proper level shifting chip, not resistors: less problems, and faster read/write access Use 3 or 4 digital pins to read and write 2Gb+ of storage!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
